# Fritzing sketch esp_garage_arrosage_esp01s (saved by Fritzing 0.9.3b)

parts:
  DHT1 = DHT22 Humidity and Temperature Sensor
  R1 = Resistor [tolerance=±5% resistance=4.7k package=THT]
  KY-1 = Keyes Relay [package=THT]
  Composant1 = LCD1602-I2C
  Espessif_Serial_Wifi_Modul_1 = ESP8266 ESP01 [part_number=ESP8266 package=THT]
  Composant2 = Adafruit 4-channel I2C-safe Bi-directional Logic Level Converter [part_number="Adafruit #757"]
  AMS1 = AMS1777 5V regulator module
  Power_plug1 = Power plug

nets:
  GND: DHT1.GND, Espessif_Serial_Wifi_Modul_1.GND, Composant2.GND
  N1: R1.Pin_0, Espessif_Serial_Wifi_Modul_1.TXD
  N2: KY-1.signal, Espessif_Serial_Wifi_Modul_1.RXD
  N3: KY-1.power, Composant2.LV
  N4: KY-1.ground, AMS1.GND-_(output)
  GND_2: Composant1.GND, AMS1.GND-_(input), Power_plug1.GND
  VCC: Composant1.VCC, Composant2.HV, AMS1.VIN+, Power_plug1.VCC
  N5: Composant1.SDA, Composant2.B1
  N6: Composant1.SCL, Composant2.B2
  N7: Espessif_Serial_Wifi_Modul_1.VCC, Espessif_Serial_Wifi_Modul_1.CH_PD, AMS1.VOUT+
  N8: Espessif_Serial_Wifi_Modul_1.GPIO00, Composant2.A1
  N9: Espessif_Serial_Wifi_Modul_1.GPIO02, Composant2.A2

notes:
  DHT22
  ESP8266 esp01s /esphome
  4.7K
  Relais EV Cuve
  5V
  3V
  AMS1117
  5V (rpi2)
  Level Shifter
  LCD 16x2 I2C (5v)

custom parts:
  Keyes Relay: The Keyes 5V relay module is suitable for SCM development, home appliance control. It uses a 5V~12V TIL control signal which can control DC / AC signal.
  LCD1602-I2C: A standard character display, usually with 2x16 characters. Comes in many colors with LCM1602 IIC attached.
  ESP8266 ESP01: Generic WiFi Module based on the ESP8266 with onboard PCB antenna and UART communications
  Adafruit 4-channel I2C-safe Bi-directional Logic Level Converter: Because the Arduino (and Basic Stamp) are 5V devices, and most modern sensors, displays, flash cards and modes are 3.3V-only, many makers find that they need to perform level shifting/conversion to protect the 3.3V device from 5V. We do have some other handy level shifters in the shop, from the DIP 74LVC245 to the fancy bi-directional TXB0108. However, neither of these are happy to work with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
  AMS1777 5V regulator module: AMS1777 5V regulator module source : https://github.com/ShenTengTu/fritzing_parts/tree/master/voltage%20regulator/AMS1117_5V_regulator_module
